// Logisim project cpu-riscv-hust-2022-team.circ as structural Verilog: 7 circuits, main circuit 团队任务
module PCType (
  input  Eq,
  input  Lt,
  input  Ge,
  input  URET,
  input  JALR,
  input  JAL,
  input  BEQ,
  input  BNE,
  input  BLT_U,
  output [1:0] JmpType,
  output Jmp,
  output ImmJmp,
  output LinkToReg,
  output UncondJmp,
  output CondBranch,
  output BranchInstr,
  output UncertainJmp
);

  wire and_1_out, and_2_out, and_3_out;

  Pull_Resistor #(.pull(0)) pull_resistor_1 (.node(JmpType));
  Priority_Encoder #(.select(2), .disabled(0)) priority_encoder_1 (
    .in1(URET), .in2(JALR), .in3(ImmJmp), .out(JmpType), .gs(Jmp));  // open: in0, en_out, en_in
  or or_1 (LinkToReg, JALR, JAL);
  or or_2 (ImmJmp, JAL, and_1_out, and_2_out, and_3_out);
  and and_1 (and_1_out, Eq, BEQ);
  or or_3 (UncertainJmp, JALR, BEQ, BNE, BLT_U);
  or or_4 (CondBranch, and_1_out, and_2_out, and_3_out);
  and and_2 (and_2_out, ~Eq, BNE);  // AND_Gate
  and and_3 (and_3_out, Lt, BLT_U);
  or or_5 (BranchInstr, BLT_U, BNE, BEQ);

  assign UncondJmp = LinkToReg;
endmodule

// 单周期硬布线控制器
module \单周期硬布线控制器  (
  input  [4:0] OP,
  input  [4:0] Funct,
  input  in_3,
  input  [1:0] LegitIR,
  output [3:0] ALU_OP,
  output ALU_RESULT,
  output uret,
  output MemToReg,
  output ecall,
  output MemWrite,
  output AluSrcB,
  output AluSrcA,
  output RegWrite,
  output S_type,
  output U_type,
  output Beq,
  output Bne,
  output JALR,
  output JAL,
  output Blt_u,
  output R1Dep,
  output [2:0] Func3,
  output R2Dep,
  output CSR
);

  wire and_1_out, \控制信号自动生成_1_ecall ;

  and and_1 (and_1_out, LegitIR[0], LegitIR[1]);
  \运算控制器自动生成  \u_运算控制器自动生成_1  (
    .OP2(OP[0]), .OP3(OP[1]), .OP4(OP[2]), .OP5(OP[3]), .OP6(OP[4]), .F12(Funct[0]), .F13(Funct[1]),
    .F14(Funct[2]), .F25(Funct[3]), .F30(Funct[4]), .S0(ALU_OP[0]), .S1(ALU_OP[1]), .S2(ALU_OP[2]),
    .S3(ALU_OP[3]), .RE(ALU_RESULT));
  \控制信号自动生成  \u_控制信号自动生成_1  (
    .OP2(OP[0]), .OP3(OP[1]), .MemToReg(MemToReg), .OP4(OP[2]), .OP5(OP[3]), .OP6(OP[4]),
    .MemWrite(MemWrite), .F12(Funct[0]), .F13(Funct[1]), .F14(Funct[2]), .F25(Funct[3]), .F30(Funct[4]),
    .EN(and_1_out), .AluSrcB(AluSrcB), .AluSrcA(AluSrcA), .RegWrite(RegWrite), .ecall(\控制信号自动生成_1_ecall ),
    .S_Type(S_type), .U_Type(U_type), .BEQ(Beq), .BNE(Bne), .JALR(JALR), .JAL(JAL), .BLTU(Blt_u),
    .R1Dep(R1Dep), .R2Dep(R2Dep), .CSR(CSR));
  and and_2 (uret, in_3, \控制信号自动生成_1_ecall );
  and and_3 (ecall, ~in_3, \控制信号自动生成_1_ecall );  // AND_Gate

  assign Func3 = Funct[2:0];

  // Other names for the same wires on the sheet: IR21 = in_3; OP_CODE[4:0] = OP

  // Notes on the sheet:
  //   控制信号生成，产生数据通路需要的其他控制信号
  //   运算器控制器，根据指令生成运算器功能选择信号
endmodule

// 运算器控制器
module \运算控制器自动生成  (
  input  OP2,
  input  OP3,
  input  OP4,
  input  OP5,
  input  OP6,
  input  F12,
  input  F13,
  input  F14,
  input  F25,
  input  F30,
  output S0,
  output S1,
  output S2,
  output S3,
  output RE
);

  wire and_1_out, and_2_out, and_3_out, and_4_out, and_5_out, and_6_out, and_7_out, and_8_out, and_9_out,
       and_10_out, and_11_out, and_12_out, and_13_out, and_14_out, and_15_out, and_16_out, and_17_out,
       and_18_out, and_19_out, and_20_out, and_21_out, and_22_out, and_23_out, and_24_out, and_25_out,
       and_26_out, and_27_out, and_28_out, and_29_out, and_30_out, and_31_out, and_32_out, and_33_out,
       and_34_out, and_35_out, and_36_out, and_37_out, and_38_out, and_39_out, and_40_out, and_41_out,
       and_42_out, and_43_out, and_44_out, not_1_out, not_2_out, not_3_out, not_4_out, not_5_out, not_6_out,
       not_7_out, not_8_out, not_9_out, not_10_out, not_11_out, not_12_out, not_13_out, not_14_out,
       not_15_out, not_16_out, not_17_out, not_18_out, not_19_out, not_20_out, not_21_out, not_22_out,
       not_23_out, not_24_out, not_25_out, not_26_out, not_27_out, not_28_out, not_29_out, not_30_out,
       not_31_out, not_32_out, not_33_out, not_34_out, not_35_out, not_36_out, not_37_out, not_38_out,
       not_39_out, not_40_out, not_41_out, not_42_out, not_43_out, not_44_out, not_45_out, not_46_out,
       not_47_out, not_48_out, not_49_out, not_50_out, not_51_out, not_52_out, not_53_out, not_54_out,
       not_55_out, not_56_out, not_57_out, not_58_out, not_59_out, not_60_out, not_61_out, not_62_out,
       not_63_out, not_64_out, not_65_out, not_66_out, not_67_out, not_68_out, not_69_out, not_70_out,
       not_71_out, not_72_out, not_73_out, not_74_out, not_75_out, not_76_out, not_77_out, not_78_out,
       not_79_out, not_80_out, not_81_out, not_82_out, not_83_out, not_84_out, not_85_out, not_86_out,
       not_87_out, not_88_out, not_89_out, not_90_out, not_91_out, not_92_out, not_93_out, not_94_out,
       not_95_out, not_96_out, not_97_out, not_98_out, not_99_out, not_100_out, not_101_out, not_102_out,
       not_103_out, not_104_out, not_105_out, not_106_out, not_107_out, not_108_out, not_109_out,
       not_110_out, not_111_out, not_112_out, not_113_out, not_114_out, not_115_out, not_116_out,
       not_117_out, not_118_out, not_119_out, not_120_out, not_121_out, not_122_out, not_123_out,
       not_124_out, not_125_out, not_126_out, not_127_out, not_128_out, not_129_out, not_130_out,
       not_131_out, not_132_out, not_133_out, not_134_out, not_135_out, not_136_out, not_137_out,
       not_138_out, not_139_out, not_140_out, not_141_out, not_142_out, not_143_out, not_144_out,
       not_145_out, not_146_out, not_147_out, not_148_out, not_149_out, not_150_out, not_151_out,
       not_152_out, not_153_out, not_154_out, not_155_out, not_156_out, not_157_out, not_158_out,
       not_159_out, not_160_out, not_161_out, not_162_out, not_163_out, not_164_out, not_165_out,
       not_166_out, not_167_out, not_168_out, not_169_out, not_170_out, not_171_out, not_172_out,
       not_173_out, not_174_out, not_175_out, not_176_out, not_177_out, not_178_out, not_179_out,
       not_180_out, not_181_out, not_182_out, not_183_out, not_184_out, not_185_out, not_186_out,
       not_187_out, not_188_out, not_189_out, not_190_out, not_191_out, not_192_out, not_193_out,
       not_194_out, not_195_out, not_196_out, not_197_out, not_198_out, not_199_out, not_200_out,
       not_201_out, not_202_out, not_203_out, not_204_out, not_205_out, not_206_out, not_207_out,
       not_208_out, not_209_out, not_210_out, not_211_out, not_212_out, not_213_out, not_214_out,
       not_215_out, not_216_out, not_217_out, not_218_out, not_219_out, not_220_out, not_221_out,
       not_222_out, not_223_out, not_224_out, not_225_out, not_226_out, not_227_out, not_228_out,
       not_229_out, not_230_out, not_231_out, not_232_out, not_233_out, not_234_out, not_235_out;

  not not_1 (not_1_out, F30);
  not not_2 (not_2_out, F25);
  not not_3 (not_3_out, F14);
  not not_4 (not_4_out, F13);
  not not_5 (not_5_out, F12);
  not not_6 (not_6_out, OP6);
  not not_7 (not_7_out, OP3);
  not not_8 (not_8_out, OP2);
  not not_9 (not_9_out, F30);
  not not_10 (not_10_out, F25);
  not not_11 (not_11_out, OP6);
  not not_12 (not_12_out, OP3);
  not not_13 (not_13_out, OP2);
  not not_14 (not_14_out, F30);
  not not_15 (not_15_out, F25);
  not not_16 (not_16_out, F14);
  not not_17 (not_17_out, F12);
  not not_18 (not_18_out, OP6);
  not not_19 (not_19_out, OP3);
  not not_20 (not_20_out, OP2);
  not not_21 (not_21_out, F14);
  not not_22 (not_22_out, F13);
  not not_23 (not_23_out, F12);
  not not_24 (not_24_out, OP6);
  not not_25 (not_25_out, OP5);
  not not_26 (not_26_out, OP3);
  not not_27 (not_27_out, OP2);
  not not_28 (not_28_out, OP6);
  not not_29 (not_29_out, OP5);
  not not_30 (not_30_out, OP3);
  not not_31 (not_31_out, OP2);
  not not_32 (not_32_out, F13);
  not not_33 (not_33_out, F12);
  not not_34 (not_34_out, OP6);
  not not_35 (not_35_out, OP5);
  not not_36 (not_36_out, OP3);
  not not_37 (not_37_out, OP2);
  not not_38 (not_38_out, F14);
  not not_39 (not_39_out, OP6);
  not not_40 (not_40_out, OP5);
  not not_41 (not_41_out, OP3);
  not not_42 (not_42_out, OP2);
  not not_43 (not_43_out, F25);
  not not_44 (not_44_out, F13);
  not not_45 (not_45_out, OP6);
  not not_46 (not_46_out, OP5);
  not not_47 (not_47_out, OP3);
  not not_48 (not_48_out, OP2);
  not not_49 (not_49_out, OP6);
  not not_50 (not_50_out, OP5);
  not not_51 (not_51_out, OP4);
  not not_52 (not_52_out, OP3);
  not not_53 (not_53_out, OP2);
  not not_54 (not_54_out, F14);
  not not_55 (not_55_out, F12);
  not not_56 (not_56_out, OP6);
  not not_57 (not_57_out, OP4);
  not not_58 (not_58_out, OP3);
  not not_59 (not_59_out, OP2);
  not not_60 (not_60_out, F14);
  not not_61 (not_61_out, F13);
  not not_62 (not_62_out, F12);
  not not_63 (not_63_out, OP4);
  not not_64 (not_64_out, OP3);
  not not_65 (not_65_out, F13);
  not not_66 (not_66_out, F12);
  not not_67 (not_67_out, OP4);
  not not_68 (not_68_out, OP3);
  not not_69 (not_69_out, OP2);
  not not_70 (not_70_out, OP6);
  not not_71 (not_71_out, OP5);
  not not_72 (not_72_out, OP3);
  not not_73 (not_73_out, F25);
  not not_74 (not_74_out, F14);
  not not_75 (not_75_out, F13);
  not not_76 (not_76_out, F12);
  not not_77 (not_77_out, OP6);
  not not_78 (not_78_out, OP3);
  not not_79 (not_79_out, OP2);
  not not_80 (not_80_out, F30);
  not not_81 (not_81_out, F25);
  not not_82 (not_82_out, OP6);
  not not_83 (not_83_out, OP3);
  not not_84 (not_84_out, OP2);
  not not_85 (not_85_out, F30);
  not not_86 (not_86_out, F25);
  not not_87 (not_87_out, F14);
  not not_88 (not_88_out, F12);
  not not_89 (not_89_out, OP6);
  not not_90 (not_90_out, OP3);
  not not_91 (not_91_out, OP2);
  not not_92 (not_92_out, OP6);
  not not_93 (not_93_out, OP5);
  not not_94 (not_94_out, OP3);
  not not_95 (not_95_out, OP2);
  not not_96 (not_96_out, F14);
  not not_97 (not_97_out, OP6);
  not not_98 (not_98_out, OP5);
  not not_99 (not_99_out, OP3);
  not not_100 (not_100_out, OP2);
  not not_101 (not_101_out, F30);
  not not_102 (not_102_out, F25);
  not not_103 (not_103_out, F13);
  not not_104 (not_104_out, OP6);
  not not_105 (not_105_out, OP5);
  not not_106 (not_106_out, OP3);
  not not_107 (not_107_out, OP2);
  not not_108 (not_108_out, F13);
  not not_109 (not_109_out, F12);
  not not_110 (not_110_out, OP4);
  not not_111 (not_111_out, OP3);
  not not_112 (not_112_out, OP2);
  not not_113 (not_113_out, OP6);
  not not_114 (not_114_out, OP3);
  not not_115 (not_115_out, F30);
  not not_116 (not_116_out, F25);
  not not_117 (not_117_out, F14);
  not not_118 (not_118_out, F13);
  not not_119 (not_119_out, F12);
  not not_120 (not_120_out, OP6);
  not not_121 (not_121_out, OP3);
  not not_122 (not_122_out, OP2);
  not not_123 (not_123_out, F25);
  not not_124 (not_124_out, F14);
  not not_125 (not_125_out, F13);
  not not_126 (not_126_out, F12);
  not not_127 (not_127_out, OP6);
  not not_128 (not_128_out, OP3);
  not not_129 (not_129_out, OP2);
  not not_130 (not_130_out, F30);
  not not_131 (not_131_out, F25);
  not not_132 (not_132_out, OP6);
  not not_133 (not_133_out, OP3);
  not not_134 (not_134_out, OP2);
  not not_135 (not_135_out, F30);
  not not_136 (not_136_out, F25);
  not not_137 (not_137_out, F14);
  not not_138 (not_138_out, OP6);
  not not_139 (not_139_out, OP3);
  not not_140 (not_140_out, OP2);
  not not_141 (not_141_out, F14);
  not not_142 (not_142_out, F13);
  not not_143 (not_143_out, F12);
  not not_144 (not_144_out, OP6);
  not not_145 (not_145_out, OP5);
  not not_146 (not_146_out, OP3);
  not not_147 (not_147_out, OP2);
  not not_148 (not_148_out, OP6);
  not not_149 (not_149_out, OP5);
  not not_150 (not_150_out, OP3);
  not not_151 (not_151_out, OP2);
  not not_152 (not_152_out, OP6);
  not not_153 (not_153_out, OP5);
  not not_154 (not_154_out, OP4);
  not not_155 (not_155_out, OP3);
  not not_156 (not_156_out, OP2);
  not not_157 (not_157_out, F14);
  not not_158 (not_158_out, F12);
  not not_159 (not_159_out, OP6);
  not not_160 (not_160_out, OP4);
  not not_161 (not_161_out, OP3);
  not not_162 (not_162_out, OP2);
  not not_163 (not_163_out, F14);
  not not_164 (not_164_out, F13);
  not not_165 (not_165_out, F12);
  not not_166 (not_166_out, OP4);
  not not_167 (not_167_out, OP3);
  not not_168 (not_168_out, F30);
  not not_169 (not_169_out, F13);
  not not_170 (not_170_out, OP6);
  not not_171 (not_171_out, OP3);
  not not_172 (not_172_out, OP2);
  not not_173 (not_173_out, F30);
  not not_174 (not_174_out, OP6);
  not not_175 (not_175_out, OP3);
  not not_176 (not_176_out, OP2);
  not not_177 (not_177_out, F12);
  not not_178 (not_178_out, OP4);
  not not_179 (not_179_out, OP3);
  not not_180 (not_180_out, OP2);
  not not_181 (not_181_out, OP6);
  not not_182 (not_182_out, OP3);
  not not_183 (not_183_out, OP6);
  not not_184 (not_184_out, OP5);
  not not_185 (not_185_out, OP3);
  not not_186 (not_186_out, F30);
  not not_187 (not_187_out, F25);
  not not_188 (not_188_out, F12);
  not not_189 (not_189_out, OP6);
  not not_190 (not_190_out, OP3);
  not not_191 (not_191_out, OP2);
  not not_192 (not_192_out, F30);
  not not_193 (not_193_out, F25);
  not not_194 (not_194_out, F14);
  not not_195 (not_195_out, F12);
  not not_196 (not_196_out, OP6);
  not not_197 (not_197_out, OP3);
  not not_198 (not_198_out, OP2);
  not not_199 (not_199_out, F30);
  not not_200 (not_200_out, F25);
  not not_201 (not_201_out, F14);
  not not_202 (not_202_out, OP6);
  not not_203 (not_203_out, OP3);
  not not_204 (not_204_out, OP2);
  not not_205 (not_205_out, F12);
  not not_206 (not_206_out, OP6);
  not not_207 (not_207_out, OP5);
  not not_208 (not_208_out, OP3);
  not not_209 (not_209_out, OP2);
  not not_210 (not_210_out, F13);
  not not_211 (not_211_out, F12);
  not not_212 (not_212_out, OP6);
  not not_213 (not_213_out, OP5);
  not not_214 (not_214_out, OP3);
  not not_215 (not_215_out, OP2);
  not not_216 (not_216_out, F14);
  not not_217 (not_217_out, OP6);
  not not_218 (not_218_out, OP5);
  not not_219 (not_219_out, OP3);
  not not_220 (not_220_out, OP2);
  not not_221 (not_221_out, F12);
  not not_222 (not_222_out, OP4);
  not not_223 (not_223_out, OP3);
  not not_224 (not_224_out, OP2);
  not not_225 (not_225_out, F13);
  not not_226 (not_226_out, F12);
  not not_227 (not_227_out, OP4);
  not not_228 (not_228_out, OP3);
  not not_229 (not_229_out, OP2);
  not not_230 (not_230_out, OP6);
  not not_231 (not_231_out, OP3);
  not not_232 (not_232_out, F30);
  not not_233 (not_233_out, OP6);
  not not_234 (not_234_out, OP3);
  not not_235 (not_235_out, OP2);
  and and_1 (and_1_out, not_1_out, not_2_out, not_3_out, not_4_out, not_5_out, not_6_out, OP5, OP4, not_7_out, not_8_out);
  and and_2 (and_2_out, not_9_out, not_10_out, F14, F13, F12, not_11_out, OP5, OP4, not_12_out, not_13_out);
  and and_3 (and_3_out, not_14_out, not_15_out, not_16_out, F13, not_17_out, not_18_out, OP5, OP4, not_19_out, not_20_out);
  and and_4 (and_4_out, not_21_out, not_22_out, not_23_out, not_24_out, not_25_out, OP4, not_26_out, not_27_out);
  and and_5 (and_5_out, F14, F13, F12, not_28_out, not_29_out, OP4, not_30_out, not_31_out);
  and and_6 (and_6_out, F14, not_32_out, not_33_out, not_34_out, not_35_out, OP4, not_36_out, not_37_out);
  and and_7 (and_7_out, not_38_out, F13, F12, not_39_out, not_40_out, OP4, not_41_out, not_42_out);
  and and_8 (and_8_out, F30, not_43_out, F14, not_44_out, F12, not_45_out, not_46_out, OP4, not_47_out, not_48_out);
  and and_9 (and_9_out, not_49_out, not_50_out, not_51_out, not_52_out, not_53_out);
  and and_10 (and_10_out, not_54_out, F13, not_55_out, not_56_out, OP5, not_57_out, not_58_out, not_59_out);
  and and_11 (and_11_out, not_60_out, not_61_out, not_62_out, OP6, OP5, not_63_out, not_64_out, OP2);
  and and_12 (and_12_out, F14, not_65_out, not_66_out, OP6, OP5, not_67_out, not_68_out, not_69_out);
  and and_13 (and_13_out, not_70_out, not_71_out, OP4, not_72_out, OP2);
  and and_14 (and_14_out, F30, not_73_out, not_74_out, not_75_out, not_76_out, not_77_out, OP5, OP4, not_78_out, not_79_out);
  and and_15 (and_15_out, not_80_out, not_81_out, F14, F13, F12, not_82_out, OP5, OP4, not_83_out, not_84_out);
  and and_16 (and_16_out, not_85_out, not_86_out, not_87_out, F13, not_88_out, not_89_out, OP5, OP4, not_90_out, not_91_out);
  and and_17 (and_17_out, F14, F13, F12, not_92_out, not_93_out, OP4, not_94_out, not_95_out);
  and and_18 (and_18_out, not_96_out, F13, F12, not_97_out, not_98_out, OP4, not_99_out, not_100_out);
  and and_19 (and_19_out, not_101_out, not_102_out, F14, not_103_out, F12, not_104_out, not_105_out, OP4, not_106_out, not_107_out);
  and and_20 (and_20_out, F14, not_108_out, not_109_out, OP6, OP5, not_110_out, not_111_out, not_112_out);
  and and_21 (and_21_out, not_113_out, OP5, OP4, not_114_out, OP2);
  and and_22 (and_22_out, not_115_out, not_116_out, not_117_out, not_118_out, not_119_out, not_120_out, OP5, OP4, not_121_out, not_122_out);
  and and_23 (and_23_out, F30, not_123_out, not_124_out, not_125_out, not_126_out, not_127_out, OP5, OP4, not_128_out, not_129_out);
  and and_24 (and_24_out, not_130_out, not_131_out, F14, F13, F12, not_132_out, OP5, OP4, not_133_out, not_134_out);
  and and_25 (and_25_out, not_135_out, not_136_out, not_137_out, F13, F12, not_138_out, OP5, OP4, not_139_out, not_140_out);
  and and_26 (and_26_out, not_141_out, not_142_out, not_143_out, not_144_out, not_145_out, OP4, not_146_out, not_147_out);
  and and_27 (and_27_out, F14, F13, F12, not_148_out, not_149_out, OP4, not_150_out, not_151_out);
  and and_28 (and_28_out, not_152_out, not_153_out, not_154_out, not_155_out, not_156_out);
  and and_29 (and_29_out, not_157_out, F13, not_158_out, not_159_out, OP5, not_160_out, not_161_out, not_162_out);
  and and_30 (and_30_out, not_163_out, not_164_out, not_165_out, OP6, OP5, not_166_out, not_167_out, OP2);
  and and_31 (and_31_out, not_168_out, F25, F14, not_169_out, F12, not_170_out, OP5, OP4, not_171_out, not_172_out);
  and and_32 (and_32_out, not_173_out, F25, F14, F13, F12, not_174_out, OP5, OP4, not_175_out, not_176_out);
  and and_33 (and_33_out, F14, F13, not_177_out, OP6, OP5, not_178_out, not_179_out, not_180_out);
  and and_34 (and_34_out, not_181_out, OP5, OP4, not_182_out, OP2);
  and and_35 (and_35_out, not_183_out, not_184_out, OP4, not_185_out, OP2);
  and and_36 (and_36_out, not_186_out, not_187_out, F14, F13, not_188_out, not_189_out, OP5, OP4, not_190_out, not_191_out);
  and and_37 (and_37_out, not_192_out, not_193_out, not_194_out, F13, not_195_out, not_196_out, OP5, OP4, not_197_out, not_198_out);
  and and_38 (and_38_out, not_199_out, not_200_out, not_201_out, F13, F12, not_202_out, OP5, OP4, not_203_out, not_204_out);
  and and_39 (and_39_out, F14, F13, not_205_out, not_206_out, not_207_out, OP4, not_208_out, not_209_out);
  and and_40 (and_40_out, F14, not_210_out, not_211_out, not_212_out, not_213_out, OP4, not_214_out, not_215_out);
  and and_41 (and_41_out, not_216_out, F13, F12, not_217_out, not_218_out, OP4, not_219_out, not_220_out);
  and and_42 (and_42_out, F14, F13, not_221_out, OP6, OP5, not_222_out, not_223_out, not_224_out);
  and and_43 (and_43_out, F14, not_225_out, not_226_out, OP6, OP5, not_227_out, not_228_out, not_229_out);
  and and_44 (and_44_out, not_230_out, OP5, OP4, not_231_out, OP2);
  and and_45 (RE, not_232_out, F25, F14, F13, F12, not_233_out, OP5, OP4, not_234_out, not_235_out);
  or or_1 (S0, and_1_out, and_2_out, and_3_out, and_4_out, and_5_out, and_6_out, and_7_out, and_8_out, and_9_out, and_10_out, and_11_out, and_12_out, and_13_out);
  or or_2 (S1, and_14_out, and_15_out, and_16_out, and_17_out, and_18_out, and_19_out, and_20_out, and_21_out);
  or or_3 (S2, and_22_out, and_23_out, and_24_out, and_25_out, and_26_out, and_27_out, and_28_out, and_29_out, and_30_out, and_31_out, and_32_out, and_33_out, and_34_out, and_35_out);
  or or_4 (S3, and_36_out, and_37_out, and_38_out, and_39_out, and_40_out, and_41_out, and_42_out, and_43_out, and_44_out);
endmodule

// 控制信号生成
module \控制信号自动生成  (
  input  OP2,
  input  OP3,
  input  OP4,
  input  OP5,
  input  OP6,
  input  F12,
  input  F13,
  input  F14,
  input  F25,
  input  F30,
  input  EN,
  output MemToReg,
  output MemWrite,
  output AluSrcB,
  output AluSrcA,
  output RegWrite,
  output ecall,
  output S_Type,
  output U_Type,
  output BEQ,
  output BNE,
  output JALR,
  output JAL,
  output BLTU,
  output R1Dep,
  output R2Dep,
  output CSR
);

  wire and_6_out, and_7_out, and_8_out, and_9_out, and_10_out, and_11_out, and_12_out, and_13_out,
       and_14_out, and_15_out, and_16_out, and_17_out, and_18_out, and_19_out, and_20_out, and_21_out,
       and_22_out, and_23_out, and_24_out, and_25_out, and_32_out, and_33_out, and_34_out, and_35_out,
       and_36_out, and_37_out, and_38_out, and_39_out, and_40_out, and_41_out, and_42_out, and_43_out,
       and_44_out, and_45_out, and_46_out, and_47_out, and_48_out, and_49_out, and_50_out, and_51_out,
       and_52_out, and_53_out, not_1_out, not_2_out, not_3_out, not_4_out, not_5_out, not_6_out, not_7_out,
       not_8_out, not_9_out, not_10_out, not_11_out, not_12_out, not_13_out, not_14_out, not_15_out,
       not_16_out, not_17_out, not_18_out, not_19_out, not_20_out, not_21_out, not_22_out, not_23_out,
       not_24_out, not_25_out, not_26_out, not_27_out, not_28_out, not_29_out, not_30_out, not_31_out,
       not_32_out, not_33_out, not_34_out, not_35_out, not_36_out, not_37_out, not_38_out, not_39_out,
       not_40_out, not_41_out, not_42_out, not_43_out, not_44_out, not_45_out, not_46_out, not_47_out,
       not_48_out, not_49_out, not_50_out, not_51_out, not_52_out, not_53_out, not_54_out, not_55_out,
       not_56_out, not_57_out, not_58_out, not_59_out, not_60_out, not_61_out, not_62_out, not_63_out,
       not_64_out, not_65_out, not_66_out, not_67_out, not_68_out, not_69_out, not_70_out, not_71_out,
       not_72_out, not_73_out, not_74_out, not_75_out, not_76_out, not_77_out, not_78_out, not_79_out,
       not_80_out, not_81_out, not_82_out, not_83_out, not_84_out, not_85_out, not_86_out, not_87_out,
       not_88_out, not_89_out, not_90_out, not_91_out, not_92_out, not_93_out, not_94_out, not_95_out,
       not_96_out, not_97_out, not_98_out, not_99_out, not_100_out, not_101_out, not_102_out, not_103_out,
       not_104_out, not_105_out, not_106_out, not_107_out, not_108_out, not_109_out, not_110_out,
       not_111_out, not_112_out, not_113_out, not_114_out, not_115_out, not_116_out, not_117_out,
       not_118_out, not_119_out, not_120_out, not_121_out, not_122_out, not_123_out, not_124_out,
       not_125_out, not_126_out, not_127_out, not_128_out, not_129_out, not_130_out, not_131_out,
       not_132_out, not_133_out, not_134_out, not_135_out, not_136_out, not_137_out, not_138_out,
       not_139_out, not_140_out, not_141_out, not_142_out, not_143_out, not_144_out, not_145_out,
       not_146_out, not_147_out, not_148_out, not_149_out, not_150_out, not_151_out, not_152_out,
       not_153_out, not_154_out, not_155_out, not_156_out, not_157_out, not_158_out, not_159_out,
       not_160_out, not_161_out, not_162_out, not_163_out, not_164_out, not_165_out, not_166_out,
       not_167_out, not_168_out, not_169_out, not_170_out, not_171_out, not_172_out, not_173_out,
       not_174_out, not_175_out, not_176_out, not_177_out, not_178_out, not_179_out, not_180_out,
       not_181_out, not_182_out, not_183_out, not_184_out, not_185_out, not_186_out, not_187_out,
       not_188_out, not_189_out, not_190_out, not_191_out, not_192_out, not_193_out, not_194_out,
       not_195_out, not_196_out, not_197_out, not_198_out, not_199_out, not_200_out, not_201_out,
       not_202_out, not_203_out, not_204_out, not_205_out, not_206_out, not_207_out, not_208_out,
       not_209_out, not_210_out, not_211_out, not_212_out, not_213_out, not_214_out, not_215_out,
       not_216_out, not_217_out, not_218_out, not_219_out, not_220_out, not_221_out, not_222_out,
       not_223_out, not_224_out, not_225_out, not_226_out, not_227_out, not_228_out, not_229_out,
       not_230_out, not_231_out, not_232_out, not_233_out, not_234_out, not_235_out, not_236_out,
       not_237_out, not_238_out, not_239_out, not_240_out, not_241_out, not_242_out, not_243_out,
       not_244_out, not_245_out, not_246_out, not_247_out, not_248_out, not_249_out, not_250_out, not_251_out;

  not not_1 (not_1_out, OP2);
  not not_2 (not_2_out, OP3);
  not not_3 (not_3_out, OP4);
  not not_4 (not_4_out, OP5);
  not not_5 (not_5_out, OP6);
  not not_6 (not_6_out, OP2);
  not not_7 (not_7_out, OP3);
  not not_8 (not_8_out, OP4);
  not not_9 (not_9_out, OP6);
  not not_10 (not_10_out, F12);
  not not_11 (not_11_out, F14);
  not not_12 (not_12_out, OP2);
  not not_13 (not_13_out, OP3);
  not not_14 (not_14_out, OP4);
  not not_15 (not_15_out, OP5);
  not not_16 (not_16_out, OP6);
  not not_17 (not_17_out, OP2);
  not not_18 (not_18_out, OP3);
  not not_19 (not_19_out, OP5);
  not not_20 (not_20_out, OP6);
  not not_21 (not_21_out, F13);
  not not_22 (not_22_out, F14);
  not not_23 (not_23_out, OP2);
  not not_24 (not_24_out, OP3);
  not not_25 (not_25_out, OP5);
  not not_26 (not_26_out, OP6);
  not not_27 (not_27_out, F12);
  not not_28 (not_28_out, OP2);
  not not_29 (not_29_out, OP3);
  not not_30 (not_30_out, OP5);
  not not_31 (not_31_out, OP6);
  not not_32 (not_32_out, F25);
  not not_33 (not_33_out, OP2);
  not not_34 (not_34_out, OP3);
  not not_35 (not_35_out, OP4);
  not not_36 (not_36_out, OP6);
  not not_37 (not_37_out, F12);
  not not_38 (not_38_out, F14);
  not not_39 (not_39_out, OP3);
  not not_40 (not_40_out, OP5);
  not not_41 (not_41_out, OP6);
  not not_42 (not_42_out, OP3);
  not not_43 (not_43_out, OP4);
  not not_44 (not_44_out, F12);
  not not_45 (not_45_out, F13);
  not not_46 (not_46_out, F14);
  not not_47 (not_47_out, OP3);
  not not_48 (not_48_out, OP5);
  not not_49 (not_49_out, OP6);
  not not_50 (not_50_out, OP2);
  not not_51 (not_51_out, OP3);
  not not_52 (not_52_out, OP4);
  not not_53 (not_53_out, OP5);
  not not_54 (not_54_out, OP6);
  not not_55 (not_55_out, OP2);
  not not_56 (not_56_out, OP3);
  not not_57 (not_57_out, OP5);
  not not_58 (not_58_out, OP6);
  not not_59 (not_59_out, F12);
  not not_60 (not_60_out, F13);
  not not_61 (not_61_out, OP2);
  not not_62 (not_62_out, OP3);
  not not_63 (not_63_out, OP5);
  not not_64 (not_64_out, OP6);
  not not_65 (not_65_out, F12);
  not not_66 (not_66_out, OP2);
  not not_67 (not_67_out, OP3);
  not not_68 (not_68_out, OP5);
  not not_69 (not_69_out, OP6);
  not not_70 (not_70_out, F25);
  not not_71 (not_71_out, OP2);
  not not_72 (not_72_out, OP3);
  not not_73 (not_73_out, OP5);
  not not_74 (not_74_out, OP6);
  not not_75 (not_75_out, F14);
  not not_76 (not_76_out, OP3);
  not not_77 (not_77_out, OP6);
  not not_78 (not_78_out, F12);
  not not_79 (not_79_out, F13);
  not not_80 (not_80_out, F14);
  not not_81 (not_81_out, F25);
  not not_82 (not_82_out, OP3);
  not not_83 (not_83_out, OP5);
  not not_84 (not_84_out, OP6);
  not not_85 (not_85_out, OP3);
  not not_86 (not_86_out, OP6);
  not not_87 (not_87_out, F25);
  not not_88 (not_88_out, F30);
  not not_89 (not_89_out, OP3);
  not not_90 (not_90_out, OP6);
  not not_91 (not_91_out, F30);
  not not_92 (not_92_out, OP4);
  not not_93 (not_93_out, F12);
  not not_94 (not_94_out, F13);
  not not_95 (not_95_out, F14);
  not not_96 (not_96_out, OP4);
  not not_97 (not_97_out, F30);
  not not_98 (not_98_out, F25);
  not not_99 (not_99_out, F14);
  not not_100 (not_100_out, F13);
  not not_101 (not_101_out, F12);
  not not_102 (not_102_out, OP3);
  not not_103 (not_103_out, OP2);
  not not_104 (not_104_out, OP2);
  not not_105 (not_105_out, OP3);
  not not_106 (not_106_out, OP4);
  not not_107 (not_107_out, OP6);
  not not_108 (not_108_out, F12);
  not not_109 (not_109_out, F14);
  not not_110 (not_110_out, OP3);
  not not_111 (not_111_out, OP6);
  not not_112 (not_112_out, OP2);
  not not_113 (not_113_out, OP3);
  not not_114 (not_114_out, OP4);
  not not_115 (not_115_out, F12);
  not not_116 (not_116_out, F13);
  not not_117 (not_117_out, F14);
  not not_118 (not_118_out, OP2);
  not not_119 (not_119_out, OP3);
  not not_120 (not_120_out, OP4);
  not not_121 (not_121_out, F13);
  not not_122 (not_122_out, F14);
  not not_123 (not_123_out, OP3);
  not not_124 (not_124_out, OP4);
  not not_125 (not_125_out, F12);
  not not_126 (not_126_out, F13);
  not not_127 (not_127_out, F14);
  not not_128 (not_128_out, OP4);
  not not_129 (not_129_out, OP2);
  not not_130 (not_130_out, OP3);
  not not_131 (not_131_out, OP4);
  not not_132 (not_132_out, F12);
  not not_133 (not_133_out, OP2);
  not not_134 (not_134_out, OP3);
  not not_135 (not_135_out, OP4);
  not not_136 (not_136_out, OP6);
  not not_137 (not_137_out, F12);
  not not_138 (not_138_out, F14);
  not not_139 (not_139_out, OP2);
  not not_140 (not_140_out, OP3);
  not not_141 (not_141_out, OP4);
  not not_142 (not_142_out, F13);
  not not_143 (not_143_out, F14);
  not not_144 (not_144_out, OP3);
  not not_145 (not_145_out, OP4);
  not not_146 (not_146_out, F12);
  not not_147 (not_147_out, F13);
  not not_148 (not_148_out, F14);
  not not_149 (not_149_out, OP2);
  not not_150 (not_150_out, OP3);
  not not_151 (not_151_out, OP4);
  not not_152 (not_152_out, F12);
  not not_153 (not_153_out, OP2);
  not not_154 (not_154_out, OP3);
  not not_155 (not_155_out, OP6);
  not not_156 (not_156_out, F12);
  not not_157 (not_157_out, F13);
  not not_158 (not_158_out, F14);
  not not_159 (not_159_out, F25);
  not not_160 (not_160_out, OP2);
  not not_161 (not_161_out, OP3);
  not not_162 (not_162_out, F12);
  not not_163 (not_163_out, F13);
  not not_164 (not_164_out, F14);
  not not_165 (not_165_out, F25);
  not not_166 (not_166_out, F30);
  not not_167 (not_167_out, OP2);
  not not_168 (not_168_out, OP3);
  not not_169 (not_169_out, OP6);
  not not_170 (not_170_out, F25);
  not not_171 (not_171_out, F30);
  not not_172 (not_172_out, OP2);
  not not_173 (not_173_out, OP3);
  not not_174 (not_174_out, OP6);
  not not_175 (not_175_out, F30);
  not not_176 (not_176_out, OP2);
  not not_177 (not_177_out, OP3);
  not not_178 (not_178_out, OP2);
  not not_179 (not_179_out, OP3);
  not not_180 (not_180_out, OP4);
  not not_181 (not_181_out, OP6);
  not not_182 (not_182_out, F12);
  not not_183 (not_183_out, F14);
  not not_184 (not_184_out, OP2);
  not not_185 (not_185_out, OP3);
  not not_186 (not_186_out, OP4);
  not not_187 (not_187_out, F13);
  not not_188 (not_188_out, F14);
  not not_189 (not_189_out, OP2);
  not not_190 (not_190_out, OP3);
  not not_191 (not_191_out, OP4);
  not not_192 (not_192_out, F12);
  not not_193 (not_193_out, OP2);
  not not_194 (not_194_out, OP3);
  not not_195 (not_195_out, OP6);
  not not_196 (not_196_out, F12);
  not not_197 (not_197_out, F13);
  not not_198 (not_198_out, F14);
  not not_199 (not_199_out, F25);
  not not_200 (not_200_out, OP2);
  not not_201 (not_201_out, OP3);
  not not_202 (not_202_out, F12);
  not not_203 (not_203_out, F13);
  not not_204 (not_204_out, F14);
  not not_205 (not_205_out, F25);
  not not_206 (not_206_out, F30);
  not not_207 (not_207_out, OP2);
  not not_208 (not_208_out, OP3);
  not not_209 (not_209_out, OP6);
  not not_210 (not_210_out, F25);
  not not_211 (not_211_out, F30);
  not not_212 (not_212_out, OP2);
  not not_213 (not_213_out, OP3);
  not not_214 (not_214_out, OP6);
  not not_215 (not_215_out, F30);
  not not_216 (not_216_out, OP2);
  not not_217 (not_217_out, OP3);
  and and_1 (MemToReg, not_1_out, not_2_out, not_3_out, not_4_out, not_5_out, EN);
  not not_218 (not_218_out, OP3);
  not not_219 (not_219_out, OP6);
  and and_2 (AluSrcA, OP2, not_47_out, OP4, not_48_out, not_49_out, EN);
  not not_220 (not_220_out, OP3);
  not not_221 (not_221_out, OP6);
  and and_3 (U_Type, OP2, not_110_out, OP4, not_111_out, EN);
  and and_4 (JAL, OP2, OP3, not_128_out, OP5, OP6, EN);
  not not_222 (not_222_out, OP2);
  not not_223 (not_223_out, OP3);
  not not_224 (not_224_out, OP4);
  not not_225 (not_225_out, OP5);
  not not_226 (not_226_out, OP6);
  not not_227 (not_227_out, OP2);
  not not_228 (not_228_out, OP3);
  not not_229 (not_229_out, OP5);
  not not_230 (not_230_out, OP6);
  not not_231 (not_231_out, F12);
  not not_232 (not_232_out, F13);
  not not_233 (not_233_out, OP2);
  not not_234 (not_234_out, OP3);
  not not_235 (not_235_out, OP5);
  not not_236 (not_236_out, OP6);
  not not_237 (not_237_out, F12);
  not not_238 (not_238_out, OP2);
  not not_239 (not_239_out, OP3);
  not not_240 (not_240_out, OP5);
  not not_241 (not_241_out, OP6);
  not not_242 (not_242_out, F14);
  not not_243 (not_243_out, OP2);
  not not_244 (not_244_out, OP3);
  not not_245 (not_245_out, OP5);
  not not_246 (not_246_out, OP6);
  not not_247 (not_247_out, F25);
  not not_248 (not_248_out, OP2);
  not not_249 (not_249_out, OP3);
  not not_250 (not_250_out, OP5);
  not not_251 (not_251_out, OP6);
  and and_5 (MemWrite, not_6_out, not_7_out, not_8_out, OP5, not_9_out, not_10_out, F13, not_11_out, EN);
  and and_6 (and_6_out, not_12_out, not_13_out, not_14_out, not_15_out, not_16_out, EN);
  and and_7 (and_7_out, not_17_out, not_18_out, not_19_out, not_20_out, not_21_out, not_22_out, EN);
  and and_8 (and_8_out, not_23_out, not_24_out, not_25_out, not_26_out, not_27_out, F14, EN);
  and and_9 (and_9_out, not_28_out, not_29_out, not_30_out, not_31_out, F14, not_32_out, EN);
  and and_10 (and_10_out, not_33_out, not_34_out, not_35_out, not_36_out, not_37_out, F13, not_38_out, EN);
  and and_11 (and_11_out, not_39_out, OP4, not_40_out, not_41_out, F12, F13, EN);
  and and_12 (and_12_out, OP2, not_42_out, not_43_out, OP5, OP6, not_44_out, not_45_out, not_46_out, EN);
  and and_13 (and_13_out, OP2, not_218_out, OP4, not_219_out, EN);
  and and_14 (and_14_out, not_50_out, not_51_out, not_52_out, not_53_out, not_54_out, EN);
  and and_15 (and_15_out, not_55_out, not_56_out, not_57_out, not_58_out, not_59_out, not_60_out, EN);
  and and_16 (and_16_out, not_61_out, not_62_out, not_63_out, not_64_out, not_65_out, F14, EN);
  and and_17 (and_17_out, not_66_out, not_67_out, not_68_out, not_69_out, F14, not_70_out, EN);
  and and_18 (and_18_out, not_71_out, not_72_out, not_73_out, not_74_out, F12, not_75_out, EN);
  and and_19 (and_19_out, not_76_out, OP4, not_77_out, not_78_out, not_79_out, not_80_out, not_81_out, EN);
  and and_20 (and_20_out, not_82_out, OP4, not_83_out, not_84_out, F12, F13, EN);
  and and_21 (and_21_out, not_85_out, OP4, OP5, not_86_out, F13, not_87_out, not_88_out, EN);
  and and_22 (and_22_out, not_89_out, OP4, OP5, not_90_out, F12, F14, F25, not_91_out, EN);
  and and_23 (and_23_out, OP2, not_92_out, OP5, OP6, not_93_out, not_94_out, not_95_out, EN);
  and and_24 (and_24_out, OP2, not_220_out, OP4, not_221_out, EN);
  and and_25 (and_25_out, OP2, OP3, not_96_out, OP5, OP6, EN);
  and and_26 (ecall, not_97_out, not_98_out, not_99_out, not_100_out, not_101_out, OP6, OP5, OP4, not_102_out, not_103_out, EN);
  and and_27 (S_Type, not_104_out, not_105_out, not_106_out, OP5, not_107_out, not_108_out, F13, not_109_out, EN);
  and and_28 (BEQ, not_112_out, not_113_out, not_114_out, OP5, OP6, not_115_out, not_116_out, not_117_out, EN);
  and and_29 (BNE, not_118_out, not_119_out, not_120_out, OP5, OP6, F12, not_121_out, not_122_out, EN);
  and and_30 (JALR, OP2, not_123_out, not_124_out, OP5, OP6, not_125_out, not_126_out, not_127_out, EN);
  and and_31 (BLTU, not_129_out, not_130_out, not_131_out, OP5, OP6, not_132_out, F14, EN);
  and and_32 (and_32_out, not_222_out, not_223_out, not_224_out, not_225_out, not_226_out, EN);
  and and_33 (and_33_out, not_227_out, not_228_out, not_229_out, not_230_out, not_231_out, not_232_out, EN);
  and and_34 (and_34_out, not_233_out, not_234_out, not_235_out, not_236_out, not_237_out, F14, EN);
  and and_35 (and_35_out, not_133_out, not_134_out, not_135_out, not_136_out, not_137_out, F13, not_138_out, EN);
  and and_36 (and_36_out, not_238_out, not_239_out, not_240_out, not_241_out, F12, not_242_out, EN);
  and and_37 (and_37_out, not_243_out, not_244_out, not_245_out, not_246_out, F12, not_247_out, EN);
  and and_38 (and_38_out, not_248_out, not_249_out, not_250_out, not_251_out, F12, F13, EN);
  and and_39 (and_39_out, not_139_out, not_140_out, not_141_out, OP5, OP6, not_142_out, not_143_out, EN);
  and and_40 (and_40_out, not_144_out, not_145_out, OP5, OP6, not_146_out, not_147_out, not_148_out, EN);
  and and_41 (and_41_out, not_149_out, not_150_out, not_151_out, OP5, OP6, not_152_out, F14, EN);
  and and_42 (and_42_out, not_153_out, not_154_out, OP4, not_155_out, not_156_out, not_157_out, not_158_out, not_159_out, EN);
  and and_43 (and_43_out, not_160_out, not_161_out, OP4, OP5, not_162_out, not_163_out, not_164_out, not_165_out, not_166_out, EN);
  and and_44 (and_44_out, not_167_out, not_168_out, OP4, OP5, not_169_out, F13, not_170_out, not_171_out, EN);
  and and_45 (and_45_out, not_172_out, not_173_out, OP4, OP5, not_174_out, F12, F14, F25, not_175_out, EN);
  and and_46 (and_46_out, not_176_out, not_177_out, OP4, OP5, OP6, F13, F14, EN);
  and and_47 (and_47_out, not_178_out, not_179_out, not_180_out, OP5, not_181_out, not_182_out, F13, not_183_out, EN);
  and and_48 (and_48_out, not_184_out, not_185_out, not_186_out, OP5, OP6, not_187_out, not_188_out, EN);
  and and_49 (and_49_out, not_189_out, not_190_out, not_191_out, OP5, OP6, not_192_out, F14, EN);
  and and_50 (and_50_out, not_193_out, not_194_out, OP4, OP5, not_195_out, not_196_out, not_197_out, not_198_out, not_199_out, EN);
  and and_51 (and_51_out, not_200_out, not_201_out, OP4, OP5, not_202_out, not_203_out, not_204_out, not_205_out, not_206_out, EN);
  and and_52 (and_52_out, not_207_out, not_208_out, OP4, OP5, not_209_out, F13, not_210_out, not_211_out, EN);
  and and_53 (and_53_out, not_212_out, not_213_out, OP4, OP5, not_214_out, F12, F14, F25, not_215_out, EN);
  and and_54 (CSR, not_216_out, not_217_out, OP4, OP5, OP6, F13, F14, EN);
  or or_1 (AluSrcB, and_6_out, and_7_out, and_8_out, and_9_out, and_10_out, and_11_out, and_12_out, and_13_out);
  or or_2 (RegWrite, and_14_out, and_15_out, and_16_out, and_17_out, and_18_out, and_19_out, and_20_out, and_21_out, and_22_out, and_23_out, and_24_out, and_25_out);
  or or_3 (R1Dep, and_32_out, and_33_out, and_34_out, and_35_out, and_36_out, and_37_out, and_38_out, and_39_out, and_40_out, and_41_out, and_42_out, and_43_out, and_44_out, and_45_out, and_46_out);
  or or_4 (R2Dep, and_47_out, and_48_out, and_49_out, and_50_out, and_51_out, and_52_out, and_53_out);
endmodule

// ALU
module ALU (
  input  [31:0] X,
  input  [31:0] Y,
  input  [3:0] AluOP,
  output out_4,
  output Equal,
  output out_6,
  output [31:0] Result,
  output [31:0] Result_2
);

  wire [0:0] comparator_1_lt, comparator_2_lt;
  wire [31:0] adder_1_out, AND_out, divider_1_out, divider_1_rem, multiplier_1_cout, multiplier_1_out,
       NOR_out, OR_out, shifter_1_out, shifter_2_out, shifter_3_out, subtractor_1_out, XOR_out;

  assign AND_out = X & Y;  // AND_Gate AND, 32 bits wide
  assign OR_out = X | Y;  // OR_Gate OR, 32 bits wide
  Shifter #(.width(32), .shift("ll")) shifter_1 (.in(X), .\dist (Y[4:0]), .out(shifter_1_out));
  Shifter #(.width(32), .shift("ar")) shifter_2 (.in(X), .\dist (Y[4:0]), .out(shifter_2_out));
  Shifter #(.width(32), .shift("lr")) shifter_3 (.in(X), .\dist (Y[4:0]), .out(shifter_3_out));
  Multiplier #(.width(32)) multiplier_1 (.a(X), .b(Y), .out(multiplier_1_out), .cout(multiplier_1_cout));  // open: cin
  Divider #(.width(32)) divider_1 (.a(X), .b(Y), .out(divider_1_out), .rem(divider_1_rem));  // open: upper
  Adder #(.width(32)) adder_1 (.a(X), .b(Y), .out(adder_1_out));  // open: cin, cout
  Subtractor #(.width(32)) subtractor_1 (.a(X), .b(Y), .out(subtractor_1_out));  // open: bin, bout
  assign XOR_out = X ^ Y;  // XOR_Gate XOR, 32 bits wide
  assign NOR_out = ~(X | Y);  // NOR_Gate NOR, 32 bits wide
  Comparator #(.width(32), .mode("twosComplement")) comparator_1 (
    .a(X), .b(Y), .eq(Equal), .lt(comparator_1_lt[0]));  // open: gt
  Comparator #(.width(32), .mode("unsigned")) comparator_2 (.a(X), .b(Y), .lt(comparator_2_lt[0]));  // open: gt, eq
  Multiplexer #(.select(4), .width(32), .disabled("Z"), .enable("false")) multiplexer_1 (
    .in0(shifter_1_out), .in1(shifter_2_out), .in2(shifter_3_out), .in3(multiplier_1_out),
    .in4(divider_1_out), .in5(adder_1_out), .in6(subtractor_1_out), .in7(AND_out), .in8(OR_out),
    .in9(XOR_out), .in10(NOR_out), .in11({{31{1'b0}}, comparator_1_lt[0]}),
    .in12({{31{1'b0}}, comparator_2_lt[0]}), .in13(X), .in14(Y), .in15({32{1'b0}}), .out(Result), .sel(AluOP));
  Multiplexer #(.select(4), .width(32), .disabled("Z"), .enable("false")) multiplexer_2 (
    .in0({32{1'b0}}), .in1({32{1'b0}}), .in2({32{1'b0}}), .in3(multiplier_1_cout), .in4(divider_1_rem),
    .in5({32{1'b0}}), .in6({32{1'b0}}), .in7({32{1'b0}}), .in8({32{1'b0}}), .in9({32{1'b0}}),
    .in10({32{1'b0}}), .in11({32{1'b0}}), .in12({32{1'b0}}), .in13({32{1'b0}}), .in14({32{1'b0}}),
    .in15({32{1'b0}}), .out(Result_2), .sel(AluOP));
  Multiplexer #(.select(4), .width(1), .disabled("Z"), .enable("false")) multiplexer_3 (
    .in0(1'b0), .in1(1'b0), .in2(1'b0), .in3(1'b0), .in4(1'b0), .in5(1'b0), .in6(1'b0), .in7(1'b0),
    .in8(1'b0), .in9(1'b0), .in10(1'b0), .in11(comparator_1_lt[0]), .in12(comparator_2_lt[0]), .in13(1'b0),
    .in14(1'b0), .in15(1'b0), .out(out_6), .sel(AluOP));
  not not_1 (out_4, out_6);

  // Other names for the same wires on the sheet: Result2[31:0] = Result_2; S[3:0] = AluOP; tunnel = out_6;
  //   tunnel_t = out_4

  // Notes on the sheet:
  //   不要改变此引脚区域内容，也不要改变ALU封装形式
  //   输入引脚
  //   输出引脚
endmodule

module Regifile (
  input  [31:0] Din,
  input  Clk,
  input  WE,
  input  [4:0] R1_num,
  input  [4:0] W_num,
  input  [4:0] R2_num,
  output [31:0] R1,
  output [31:0] R2
);

  // RegisterFile registerfile_1: pin names not known; wires that end beside it: Din, Clk, WE, W_num, R1_num, R2_num, R1, R2
endmodule

module \团队任务  (
);

  wire and_1_out, CLK, comparator_1_eq, decoder_1_out0, decoder_1_out1, ecall, Eq, Ge, Go, halt, JAL,
       LinkToReg, Lt, MemWrite, not_1_out, not_2_out, RegWrite, RST, \单周期硬布线控制器_1_alu_result ,
       \单周期硬布线控制器_1_alusrca , \单周期硬布线控制器_1_alusrcb , \单周期硬布线控制器_1_beq , \单周期硬布线控制器_1_blt_u ,
       \单周期硬布线控制器_1_bne , \单周期硬布线控制器_1_jalr , \单周期硬布线控制器_1_s_type , \单周期硬布线控制器_1_u_type , \单周期硬布线控制器_1_uret ;
  wire [0:0] \单周期硬布线控制器_1_memtoreg ;
  wire [1:0] PCType, \单周期硬布线控制器_1_func3 ;
  wire [2:2] \单周期硬布线控制器_1_func3_2 ;
  wire [3:0] \单周期硬布线控制器_1_alu_op ;
  wire [4:0] multiplexer_2_out, multiplexer_3_out;
  wire [7:0] bitselector_1_out;
  wire [11:0] multiplexer_4_out;
  wire [15:0] bitselector_2_out, NXC_q;
  wire [31:0] alu_1_result_2, bit_extender_1_out, bit_extender_2_out, bit_extender_3_out, bit_extender_4_out,
       bit_extender_5_out, bit_extender_6_out, bit_extender_7_out, IR, MemAddr, multiplexer_1_out,
       multiplexer_5_out, multiplexer_6_out, multiplexer_7_out, multiplexer_8_out, multiplexer_10_out,
       multiplexer_11_out, multiplexer_12_out, multiplexer_13_out, PC, PCp4, PCRelJmp, R1, R2, ram_1_data,
       RDin, RegRelJmp, rom_2_data;

  Button \u_继续运行  (.out(Go));
  Button \u_总复位  (.out(RST));
  not not_1 (not_1_out, halt);
  Counter #(.width(16), .max('hffff), .ongoal("wrap"), .trigger("rising"), .behavior("new")) NXC (
    .count(not_1_out), .Q(NXC_q), .clk(CLK), .clr(RST));  // open: load, D, carry, preset, down
  // Probe on NXC_q
  // Probe on PCType
  Multiplexer #(.select(2), .width(32), .disabled("Z"), .enable("false")) multiplexer_1 (
    .in0(PCp4), .in2(RegRelJmp), .in3(PCRelJmp), .out(multiplexer_1_out), .sel(PCType));  // open: in1
  Adder #(.width(32)) adder_1 (.a(PC), .b(32'h4), .out(PCp4));  // open: cin, cout
  Comparator #(.width(32), .mode("twosComplement")) comparator_1 (
    .a(R2), .b(32'h23), .eq(comparator_1_eq));  // open: gt, lt
  Clock #(.highDuration(1), .lowDuration(1)) clock_1 (.out(CLK));
  // Probe on multiplexer_1_out
  Register #(.width(32), .trigger("rising"), .Select("low")) u_PC (
    .D(multiplexer_1_out), .en(not_2_out), .Q(PC), .clk(CLK), .clr(RST));
  not not_2 (not_2_out, halt);
  and and_1 (and_1_out, ecall, comparator_1_eq);
  and and_2 (halt, ~comparator_1_eq, ecall, ~Go);  // AND_Gate
  // Probe on PC
  // RiscV_Probe riscv_probe_1: pin names not known; wires that end beside it: IR
  ROM #(.addrWidth(10), .dataWidth(32), .Select("high")) rom_1 (.addr(PC[11:2]), .data(IR));
  // LCD_Video lcd_video_1: pin names not known; wires that end beside it: RST, CLK, and_1_out, R1[7:1], R1[14:8], R1[31:16]
  // Probe on IR
  PCType pctype_1 (
    .JmpType(PCType), .Eq(Eq), .Lt(Lt), .Ge(Ge), .URET(\单周期硬布线控制器_1_uret ), .JALR(\单周期硬布线控制器_1_jalr ),
    .JAL(JAL), .BEQ(\单周期硬布线控制器_1_beq ), .BNE(\单周期硬布线控制器_1_bne ), .BLT_U(\单周期硬布线控制器_1_blt_u ),
    .LinkToReg(LinkToReg));  // open: Jmp, UncondJmp, CondBranch, ImmJmp, UncertainJmp, BranchInstr
  \单周期硬布线控制器  \u_单周期硬布线控制器_1  (
    .Funct({IR[30], IR[25], IR[14:12]}), .OP(IR[6:2]), .ALU_OP(\单周期硬布线控制器_1_alu_op ),
    .MemToReg(\单周期硬布线控制器_1_memtoreg [0]), .MemWrite(MemWrite), .AluSrcB(\单周期硬布线控制器_1_alusrcb ),
    .RegWrite(RegWrite), .ecall(ecall), .S_type(\单周期硬布线控制器_1_s_type ), .JALR(\单周期硬布线控制器_1_jalr ),
    .Beq(\单周期硬布线控制器_1_beq ), .JAL(JAL), .Bne(\单周期硬布线控制器_1_bne ), .in_3(IR[21]), .uret(\单周期硬布线控制器_1_uret ),
    .Func3({\单周期硬布线控制器_1_func3_2 [2], \单周期硬布线控制器_1_func3 }), .ALU_RESULT(\单周期硬布线控制器_1_alu_result ),
    .Blt_u(\单周期硬布线控制器_1_blt_u ), .LegitIR(IR[1:0]), .AluSrcA(\单周期硬布线控制器_1_alusrca ),
    .U_type(\单周期硬布线控制器_1_u_type ));  // open: R1Dep, R2Dep, CSR
  Multiplexer #(.select(1), .width(5), .disabled("Z"), .enable("false")) multiplexer_2 (
    .in0(IR[19:15]), .in1(5'b01010), .out(multiplexer_2_out), .sel(ecall));
  Multiplexer #(.select(1), .width(5), .disabled("Z"), .enable("false")) multiplexer_3 (
    .in0(IR[24:20]), .in1(5'b10001), .out(multiplexer_3_out), .sel(ecall));
  Multiplexer #(.select(1), .width(12), .disabled("Z"), .enable("false")) multiplexer_4 (
    .in0(IR[31:20]), .in1({IR[31:25], IR[11:7]}), .out(multiplexer_4_out), .sel(\单周期硬布线控制器_1_s_type ));
  assign bit_extender_1_out = {{19{IR[31]}}, {IR[31], IR[7], IR[30:25], IR[11:8], 1'b0}};  // Bit_Extender bit_extender_1
  assign bit_extender_2_out = {{11{IR[31]}}, {IR[31], IR[19:12], IR[20], IR[30:21], 1'b0}};  // Bit_Extender bit_extender_2
  // Probe on multiplexer_2_out
  // Probe on multiplexer_3_out
  // Probe on IR[11:7]
  assign bit_extender_3_out = {{20{multiplexer_4_out[11]}}, multiplexer_4_out};  // Bit_Extender bit_extender_3
  Multiplexer #(.select(1), .width(32), .disabled("Z"), .enable("false")) multiplexer_5 (
    .in0(bit_extender_1_out), .in1(bit_extender_2_out), .out(multiplexer_5_out), .sel(JAL));
  // Probe on multiplexer_5_out
  Regifile regifile_1 (
    .Din(RDin), .Clk(CLK), .R1(R1), .R2(R2), .WE(RegWrite), .W_num(IR[11:7]), .R1_num(multiplexer_2_out),
    .R2_num(multiplexer_3_out));
  // Probe on multiplexer_6_out
  Multiplexer #(.select(1), .width(32), .disabled("Z"), .enable("false")) multiplexer_6 (
    .in0(bit_extender_3_out), .in1({IR[31:12], {12{1'b0}}}), .out(multiplexer_6_out),
    .sel(\单周期硬布线控制器_1_u_type ));
  Adder #(.width(32)) adder_2 (.a(PC), .b(multiplexer_5_out), .out(PCRelJmp));  // open: cin, cout
  Multiplexer #(.select(1), .width(32), .disabled("Z"), .enable("false")) multiplexer_7 (
    .in0(R1), .in1(PC), .out(multiplexer_7_out), .sel(\单周期硬布线控制器_1_alusrca ));
  Multiplexer #(.select(1), .width(32), .disabled("Z"), .enable("false")) multiplexer_8 (
    .in0(R2), .in1(multiplexer_6_out), .out(multiplexer_8_out), .sel(\单周期硬布线控制器_1_alusrcb ));
  // Probe on \单周期硬布线控制器_1_alu_op 
  ALU alu_1 (
    .X(multiplexer_7_out), .Y(multiplexer_8_out), .AluOP(\单周期硬布线控制器_1_alu_op ), .Equal(Eq),
    .Result(RegRelJmp), .Result_2(alu_1_result_2), .out_4(Ge), .out_6(Lt));
  Decoder #(.select(1), .tristate("false"), .disabled(0), .enable("false")) decoder_1 (
    .out0(decoder_1_out0), .out1(decoder_1_out1), .sel(MemAddr[18]));
  Multiplexer #(.select(1), .width(32), .disabled("Z"), .enable("false")) multiplexer_9 (
    .in0(RegRelJmp), .in1(alu_1_result_2), .out(MemAddr), .sel(\单周期硬布线控制器_1_alu_result ));
  // Probe on MemAddr
  BitSelector #(.width(32), .group(8)) bitselector_1 (
    .in(multiplexer_10_out), .out(bitselector_1_out), .sel(MemAddr[1:0]));
  BitSelector #(.width(32), .group(16)) bitselector_2 (
    .in(multiplexer_10_out), .out(bitselector_2_out), .sel(MemAddr[1]));
  RAM #(.addrWidth(16), .dataWidth(32), .bus("separate"), .Select("high")) ram_1 (
    .addr(MemAddr[17:2]), .din(R2), .data(ram_1_data), .str(MemWrite), .sel(decoder_1_out0), .clk(CLK),
    .clr(RST));  // open: ld
  ROM #(.addrWidth(16), .dataWidth(32), .Select("high")) rom_2 (
    .addr(MemAddr[17:2]), .data(rom_2_data), .sel(decoder_1_out1));
  assign bit_extender_4_out = {{24{bitselector_1_out[7]}}, bitselector_1_out};  // Bit_Extender bit_extender_4
  assign bit_extender_5_out = {{24{1'b0}}, bitselector_1_out};  // Bit_Extender bit_extender_5
  assign bit_extender_6_out = {{16{bitselector_2_out[15]}}, bitselector_2_out};  // Bit_Extender bit_extender_6
  assign bit_extender_7_out = {{16{1'b0}}, bitselector_2_out};  // Bit_Extender bit_extender_7
  Multiplexer #(.select(1), .width(32), .disabled("Z"), .enable("false")) multiplexer_10 (
    .in0(ram_1_data), .in1(rom_2_data), .out(multiplexer_10_out), .sel(MemAddr[18]));
  Multiplexer #(.select(1), .width(32), .disabled("Z"), .enable("false")) multiplexer_11 (
    .in0(bit_extender_4_out), .in1(bit_extender_5_out), .out(multiplexer_11_out),
    .sel(\单周期硬布线控制器_1_func3_2 [2]));
  Multiplexer #(.select(2), .width(32), .disabled("Z"), .enable("false")) multiplexer_12 (
    .in0(multiplexer_11_out), .in1(multiplexer_13_out), .in2(multiplexer_10_out), .out(multiplexer_12_out),
    .sel(\单周期硬布线控制器_1_func3 ));  // open: in3
  Multiplexer #(.select(1), .width(32), .disabled("Z"), .enable("false")) multiplexer_13 (
    .in0(bit_extender_6_out), .in1(bit_extender_7_out), .out(multiplexer_13_out),
    .sel(\单周期硬布线控制器_1_func3_2 [2]));
  // Probe on multiplexer_10_out
  // Probe on {LinkToReg, \单周期硬布线控制器_1_memtoreg [0]}
  Multiplexer #(.select(2), .width(32), .disabled("Z"), .enable("false")) multiplexer_14 (
    .in0(MemAddr), .in1(multiplexer_12_out), .in2(PCp4), .out(RDin),
    .sel({LinkToReg, \单周期硬布线控制器_1_memtoreg [0]}));  // open: in3
  // Probe on RDin

  // Notes on the sheet:
  //   指令探针
  //   指令存储器
  //   指令字
  //   contents of rom_1 (hex, n*v repeats v):
  //   8637 60613 407b7 78793 60837 80813 713 2300893 f766b3 6d503 1051513 e56533 73 270713 fec714e3 f7d793
  //   178793 f79793 107e663 407b7 78793 a00513 a00893 73 fb9ff06f
  //   JALR
  //   URET
  //   B-Imm[12:1]
  //   J-Imm[20:1]
  //   JAL
  //   Beq
  //   Bne
  //   Blt[u]
  //   MemToReg
  //   MemWrite
  //   AluOP
  //   AluResult
  //   AluSrcA
  //   AluSrcB
  //   RegWrite
  //   I-Imm[11:0]
  //   S-Imm[11:0]
  //   U-Imm[31:20]
  //   ImmType
  //   数据存储器
  //   contents of rom_2 (hex, n*v repeats v):
  //   4*1ce71ce7 16*18c618c6 12*14a514a5 4*10841084 8*1ce71ce7 4*18c618c6 4*14a514a5 4*10841084 8*18c618c6
  //   4*1ce71ce7 16*18c618c6 12*14a514a5 4*10841084 8*1ce71ce7 4*18c618c6 4*14a514a5 4*10841084 8*18c618c6
  //   4*1ce71ce7 16*18c618c6 12*14a514a5 4*10841084 8*1ce71ce7 4*18c618c6 4*14a514a5 4*10841084 8*18c618c6
  //   4*1ce71ce7 16*18c618c6 12*14a514a5 4*10841084 8*1ce71ce7 4*18c618c6 4*14a514a5 4*10841084 8*18c618c6
  //   4*1ce71ce7 16*18c618c6 12*14a514a5 4*10841084 8*1ce71ce7 4*18c618c6 4*14a514a5 4*10841084 8*18c618c6
  //   4*1ce71ce7 16*18c618c6 12*14a514a5 4*10841084 8*1ce71ce7 4*18c618c6 4*14a514a5 4*10841084 8*18c618c6
  //   4*1ce71ce7 16*18c618c6 12*14a514a5 4*10841084 8*1ce71ce7 4*18c618c6 4*14a514a5 4*10841084 8*18c618c6
  //   4*1ce71ce7 16*18c618c6 12*14a514a5 4*10841084 8*1ce71ce7 4*18c618c6 4*14a514a5 4*10841084 8*18c618c6
  //   4*1ce71ce7 12*67106710 28*67306730 8*6b306b30 8*6b2f6b2f 4*18c618c6 4*1ce71ce7 12*67106710
  //   28*67306730 8*6b306b30 8*6b2f6b2f 4*18c618c6 4*1ce71ce7 12*67106710 28*67306730 8*6b306b30
  //   8*6b2f6b2f 4*18c618c6 4*1ce71ce7 12*67106710 28*67306730 8*6b306b30 8*6b2f6b2f 4*18c618c6 4*1ce71ce7
  //   12*67106710 28*67306730 8*6b306b30 8*6b2f6b2f 4*18c618c6 4*1ce71ce7 12*67106710 28*67306730
  //   8*6b306b30 8*6b2f6b2f 4*18c618c6 4*1ce71ce7 12*67106710 28*67306730 8*6b306b30 8*6b2f6b2f 4*18c618c6
  //   4*1ce71ce7 12*67106710 28*67306730 8*6b306b30 8*6b2f6b2f 4*18c618c6 4*14a514a5 4*67306730
  //   48*10841084 4*672e672e 4*18c618c6 4*14a514a5 4*67306730 48*10841084 4*672e672e 4*18c618c6 4*14a514a5
  //   4*67306730 48*10841084 4*672e672e 4*18c618c6 4*14a514a5 4*67306730 48*10841084 4*672e672e 4*18c618c6
  //   4*14a514a5 4*67306730 48*10841084 4*672e672e 4*18c618c6 4*14a514a5 4*67306730 48*10841084 4*672e672e
  //   4*18c618c6 4*14a514a5 4*67306730 48*10841084 4*672e672e 4*18c618c6 4*14a514a5 4*67306730 48*10841084
  //   4*672e672e 4*18c618c6 4*14a514a5 4*6b306b30 4*10841084 4*7fff7fff 40*10841084 4*672e672e 8*14a514a5
  //   4*6b306b30 4*10841084 4*7fff7fff 40*10841084 4*672e672e 8*14a514a5 4*6b306b30 4*10841084 4*7fff7fff
  //   40*10841084 4*672e672e 8*14a514a5 4*6b306b30 4*10841084 4*7fff7fff 40*10841084 4*672e672e 8*14a514a5
  //   4*6b306b30 4*10841084 4*7fff7fff 40*10841084 4*672e672e 8*14a514a5 4*6b306b30 4*10841084 4*7fff7fff
  //   40*10841084 4*672e672e 8*14a514a5 4*6b306b30 4*10841084 4*7fff7fff 40*10841084 4*672e672e 8*14a514a5
  //   4*6b306b30 4*10841084 4*7fff7fff 40*10841084 4*672e672e 4*14a514a5 4*1ce71ce7 4*6b306b30 8*10841084
  //   4*7fff7fff 36*10841084 4*672e672e 4*10841084 4*1ce71ce7 4*6b306b30 8*10841084 4*7fff7fff 36*10841084
  //   4*672e672e 4*10841084 4*1ce71ce7 4*6b306b30 8*10841084 4*7fff7fff 36*10841084 4*672e672e 4*10841084
  //   4*1ce71ce7 4*6b306b30 8*10841084 4*7fff7fff 36*10841084 4*672e672e 4*10841084 4*1ce71ce7 4*6b306b30
  //   8*10841084 4*7fff7fff 36*10841084 4*672e672e 4*10841084 4*1ce71ce7 4*6b306b30 8*10841084 4*7fff7fff
  //   36*10841084 4*672e672e 4*10841084 4*1ce71ce7 4*6b306b30 8*10841084 4*7fff7fff 36*10841084 4*672e672e
  //   4*10841084 4*1ce71ce7 4*6b306b30 8*10841084 4*7fff7fff 36*10841084 4*672e672e 4*10841084 4*14a514a5
  //   4*67306730 4*10841084 4*7fff7fff 8*10841084 8*7fff7fff 24*10841084 4*672f672f 4*10841084 4*14a514a5
  //   4*67306730 4*10841084 4*7fff7fff 8*10841084 8*7fff7fff 24*10841084 4*672f672f 4*10841084 4*14a514a5
  //   4*67306730 4*10841084 4*7fff7fff 8*10841084 8*7fff7fff 24*10841084 4*672f672f 4*10841084 4*14a514a5
  //   4*67306730 4*10841084 4*7fff7fff 8*10841084 8*7fff7fff 24*10841084 4*672f672f 4*10841084 4*14a514a5
  //   4*67306730 4*10841084 4*7fff7fff 8*10841084 8*7fff7fff 24*10841084 4*672f672f 4*10841084 4*14a514a5
  //   4*67306730 4*10841084 4*7fff7fff 8*10841084 8*7fff7fff 24*10841084 4*672f672f 4*10841084 4*14a514a5
  //   4*67306730 4*10841084 4*7fff7fff 8*10841084 8*7fff7fff 24*10841084 4*672f672f 4*10841084 4*14a514a5
  //   4*67306730 4*10841084 4*7fff7fff 8*10841084 8*7fff7fff 24*10841084 4*672f672f 4*10841084 4*18c618c6
  //   4*67306730 48*10841084 4*672e672e 4*10841084 4*18c618c6 4*67306730 48*10841084 4*672e672e 4*10841084
  //   4*18c618c6 4*67306730 48*10841084 4*672e672e 4*10841084 4*18c618c6 4*67306730 48*10841084 4*672e672e
  //   4*10841084 4*18c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
endmodule
